// Logisim project datapath.circ as structural Verilog: 7 circuits, main circuit main
// EX/MEM
module main (
);

  wire ALU_Src, and_1_out, Branch, Mem_Read, Mem_to_Reg, Mem_Write, Reg_Dest, RegWr, ZeroF;
  wire [1:0] alu_op;
  wire [2:0] bit_extender_5_out;
  wire [4:0] _11_15, _16_20, _21_25, Write_Reg;
  wire [5:0] _26_31;
  wire [10:0] _0_10;
  wire [23:0] adder_2_out, bit_extender_6_out, imm2, PC, pc_1, pcIn;
  wire [31:0] ALU_output, bit_extender_1_out, data2, data_1, imm, \output , PC_q, ram_2_data, writeD;

  assign bit_extender_1_out = {{8{1'b0}}, pcIn};  // Bit_Extender bit_extender_1
  Adder #(.width(24)) adder_1 (.a(PC), .b(24'h1), .out(pc_1));  // open: cin, cout
  Register #(.width(32)) u_PC (.D(bit_extender_1_out), .Q(PC_q));  // open: en, clk, clr
  Bit_Extender #(.in_width(32), .out_width(24)) bit_extender_2 (.in(PC_q), .out(PC));
  ID_EX ID_EX ();  // open: PC, DATA_1, DATA_2, IMM, RT, RD, EX, MEM, WB, BRANCH, RT_2, RD_2, MEM_2, WB_2
  IF_ID IF_ID ();  // open: in_1, in_2, PC
  RAM #(.addrWidth(24), .dataWidth(32)) ram_1 (
    .addr(PC), .data({_26_31, _21_25, _16_20, _11_15, _0_10}));  // open: sel, clk, ld, clr
  assign imm = {{16{1'b0}}, {_11_15, _0_10}};  // Bit_Extender bit_extender_3
  EX_MEM EX_MEM ();  // open: MEM, WB, BRANCH, ZERO, ALU_RES, in_6, RD, WB_2, ALU_RES_2, RD_2
  Register_File RegFile (
    .WriteData(writeD), .RegWrite(RegWr), .ReadRegister2(_16_20), .ReadRegister1(_21_25), .ReadData2(data2),
    .ReadData1(data_1), .WriteRegister(Write_Reg));
  Multiplexer #(.width(5), .enable("false")) multiplexer_1 (
    .in0(_11_15), .in1(_16_20), .out(Write_Reg), .sel(Reg_Dest));
  Multiplexer #(.width(32), .enable("false")) multiplexer_2 (.in0(data2), .in1(imm), .out(\output ), .sel(ALU_Src));
  Control_Unit control_unit_1 (
    ._26__A(_26_31[0]), ._27__B(_26_31[1]), ._28__C(_26_31[2]), ._29__D(_26_31[3]), ._30__E(_26_31[4]),
    ._31__F(_26_31[5]), .Reg_Write(RegWr), .RegDest(Reg_Dest), .aluop1(alu_op[0]), .alu_op2(alu_op[1]),
    .Branch(Branch), .Mem_Read(Mem_Read), .Mem_To_Reg(Mem_to_Reg), .Mem_write(Mem_Write), .ALU_src(ALU_Src));
  Bit_Extender #(.in_width(32), .out_width(24)) bit_extender_4 (.in(imm), .out(imm2));
  Adder #(.width(24)) adder_2 (.a(pc_1), .b(imm2), .out(adder_2_out));  // open: cin, cout
  and and_1 (and_1_out, Branch, ZeroF);
  ALU ALU (
    .op1(data_1), .op2(\output ), .aluOP(bit_extender_5_out), .\output (ALU_output), .zero_flag(ZeroF));  // open: in_1, out_6, out_7, in_3, out_9
  assign bit_extender_5_out = {{1{1'b0}}, alu_op};  // Bit_Extender bit_extender_5
  Multiplexer #(.width(24), .enable("false")) multiplexer_3 (
    .in0(adder_2_out), .out(pcIn), .sel(and_1_out));  // open: in1
  Bit_Extender #(.in_width(32), .out_width(24)) bit_extender_6 (.in(ALU_output), .out(bit_extender_6_out));
  RAM #(.addrWidth(24), .dataWidth(32), .bus("separate")) ram_2 (
    .addr(bit_extender_6_out), .din(data2), .data(ram_2_data), .str(Mem_Write), .ld(Mem_Read));  // open: sel, clk, clr
  Multiplexer #(.width(32), .enable("false")) multiplexer_4 (
    .in0(ALU_output), .in1(ram_2_data), .out(writeD), .sel(Mem_to_Reg));

  // Other names for the same wires on the sheet: INS[31:0] = {_26_31, _21_25, _16_20, _11_15, _0_10}
endmodule

module ALU (
  input  in_1,
  input  [31:0] op1,
  input  in_3,
  input  [31:0] op2,
  input  [2:0] aluOP,
  output out_6,
  output out_7,
  output [31:0] \output ,
  output out_9,
  output zero_flag
);

  wire comparator_1_lt;
  wire [31:0] adder_1_out, and_out, bit_extender_1_out, or_out, subtractor_1_out;

  Adder #(.width(32)) adder_1 (.a(op1), .b(op2), .out(adder_1_out), .cin(in_1), .cout(out_6));
  Subtractor #(.width(32)) subtractor_1 (.a(op1), .b(op2), .out(subtractor_1_out), .bin(in_3), .bout(out_7));
  assign or_out = op1 | op2;  // OR_Gate or, 32 bits wide
  assign and_out = op1 & op2;  // AND_Gate and, 32 bits wide
  Comparator #(.width(32)) comparator_1 (.a(op1), .b(op2), .gt(out_9), .eq(zero_flag), .lt(comparator_1_lt));
  assign bit_extender_1_out = {{31{1'b0}}, comparator_1_lt};  // Bit_Extender bit_extender_1
  Multiplexer #(.select(3), .width(32), .enable("false")) multiplexer_1 (
    .in0(adder_1_out), .in1(subtractor_1_out), .in5(or_out), .in6(and_out), .in7(bit_extender_1_out),
    .out(\output ), .sel(aluOP));  // open: in2, in3, in4
endmodule

module Register_File (
  input  [31:0] WriteData,
  input  RegWrite,
  input  [4:0] WriteRegister,
  input  [4:0] ReadRegister2,
  input  [4:0] ReadRegister1,
  output [31:0] ReadData2,
  output [31:0] ReadData1
);

  wire _0, _1, _2, _3, _4, _5, _6, _7, _8, _9, _10, _11, _12, _13, _14, _15, _16, _17, _18, _19, _20, _21,
       _22, _23, _24, _25, _26, _27, _28, _29, _30, _31, c;
  wire [31:0] r0, r1, r2, r3, r4, r5, r6, r7, r8, r9, r10, r11, r12, r13, r14, r15, r16, r17, r18, r19, r20,
       r21, r22, r23, r24, r25, r26, r27, r28, r29, r30, r31;

  Decoder #(.select(5), .disabled(0)) decoder_1 (
    .out0(_0), .out1(_1), .out2(_2), .out3(_3), .out4(_4), .out5(_5), .out6(_6), .out7(_7), .out8(_8),
    .out9(_9), .out10(_10), .out11(_11), .out12(_12), .out13(_13), .out14(_14), .out15(_15), .out16(_16),
    .out17(_17), .out18(_18), .out19(_19), .out20(_20), .out21(_21), .out22(_22), .out23(_23), .out24(_24),
    .out25(_25), .out26(_26), .out27(_27), .out28(_28), .out29(_29), .out30(_30), .out31(_31),
    .sel(WriteRegister), .en(RegWrite));
  Register #(.width(32)) register_1 (.D(WriteData), .en(_0), .Q(r0), .clk(c));  // open: clr
  Register #(.width(32)) register_2 (.D(WriteData), .en(_9), .Q(r9), .clk(c));  // open: clr
  Register #(.width(32)) register_3 (.D(WriteData), .en(_21), .Q(r21), .clk(c));  // open: clr
  Register #(.width(32)) register_4 (.D(WriteData), .en(_1), .Q(r1), .clk(c));  // open: clr
  Register #(.width(32)) register_5 (.D(WriteData), .en(_10), .Q(r10), .clk(c));  // open: clr
  Register #(.width(32)) register_6 (.D(WriteData), .en(_22), .Q(r22), .clk(c));  // open: clr
  Clock clock_1 (.out(c));
  Register #(.width(32)) register_7 (.D(WriteData), .en(_11), .Q(r11), .clk(c));  // open: clr
  Register #(.width(32)) register_8 (.D(WriteData), .en(_2), .Q(r2), .clk(c));  // open: clr
  Register #(.width(32)) register_9 (.D(WriteData), .en(_23), .Q(r23), .clk(c));  // open: clr
  Register #(.width(32)) register_10 (.D(WriteData), .en(_3), .Q(r3), .clk(c));  // open: clr
  Register #(.width(32)) register_11 (.D(WriteData), .en(_12), .Q(r12), .clk(c));  // open: clr
  Register #(.width(32)) register_12 (.D(WriteData), .en(_24), .Q(r24), .clk(c));  // open: clr
  Register #(.width(32)) register_13 (.D(WriteData), .en(_4), .Q(r4), .clk(c));  // open: clr
  Register #(.width(32)) register_14 (.D(WriteData), .en(_13), .Q(r13), .clk(c));  // open: clr
  Register #(.width(32)) register_15 (.D(WriteData), .en(_25), .Q(r25), .clk(c));  // open: clr
  Register #(.width(32)) register_16 (.D(WriteData), .en(_5), .Q(r5), .clk(c));  // open: clr
  Register #(.width(32)) register_17 (.D(WriteData), .en(_14), .Q(r14), .clk(c));  // open: clr
  Register #(.width(32)) register_18 (.D(WriteData), .en(_26), .Q(r26), .clk(c));  // open: clr
  Multiplexer #(.select(5), .width(32), .enable("false")) multiplexer_1 (
    .in0(r0), .in1(r1), .in2(r2), .in3(r3), .in4(r4), .in5(r5), .in6(r6), .in7(r7), .in8(r8), .in9(r9),
    .in10(r10), .in11(r11), .in12(r12), .in13(r13), .in14(r14), .in15(r15), .in16(r16), .in17(r17),
    .in18(r18), .in19(r19), .in20(r20), .in21(r21), .in22(r22), .in23(r23), .in24(r24), .in25(r25),
    .in26(r26), .in27(r27), .in28(r28), .in29(r29), .in30(r30), .in31(r31), .out(ReadData2),
    .sel(ReadRegister2));
  Register #(.width(32)) register_19 (.D(WriteData), .en(_15), .Q(r15), .clk(c));  // open: clr
  Register #(.width(32)) register_20 (.D(WriteData), .en(_6), .Q(r6), .clk(c));  // open: clr
  Register #(.width(32)) register_21 (.D(WriteData), .en(_16), .Q(r16), .clk(c));  // open: clr
  Register #(.width(32)) register_22 (.D(WriteData), .en(_27), .Q(r27), .clk(c));  // open: clr
  Register #(.width(32)) register_23 (.D(WriteData), .en(_7), .Q(r7), .clk(c));  // open: clr
  Register #(.width(32)) register_24 (.D(WriteData), .en(_17), .Q(r17), .clk(c));  // open: clr
  Register #(.width(32)) register_25 (.D(WriteData), .en(_28), .Q(r28), .clk(c));  // open: clr
  Multiplexer #(.select(5), .width(32), .enable("false")) multiplexer_2 (
    .in0(r0), .in1(r1), .in2(r2), .in3(r3), .in4(r4), .in5(r5), .in6(r6), .in7(r7), .in8(r8), .in9(r9),
    .in10(r10), .in11(r11), .in12(r12), .in13(r13), .in14(r14), .in15(r15), .in16(r16), .in17(r17),
    .in18(r18), .in19(r19), .in20(r20), .in21(r21), .in22(r22), .in23(r23), .in24(r24), .in25(r25),
    .in26(r26), .in27(r27), .in28(r28), .in29(r29), .in30(r30), .in31(r31), .out(ReadData1),
    .sel(ReadRegister1));
  Register #(.width(32)) register_26 (.D(WriteData), .en(_18), .Q(r18), .clk(c));  // open: clr
  Register #(.width(32)) register_27 (.D(WriteData), .en(_29), .Q(r29), .clk(c));  // open: clr
  Register #(.width(32)) register_28 (.D(WriteData), .en(_8), .Q(r8), .clk(c));  // open: clr
  Register #(.width(32)) register_29 (.D(WriteData), .en(_30), .Q(r30), .clk(c));  // open: clr
  Register #(.width(32)) register_30 (.D(WriteData), .en(_19), .Q(r19), .clk(c));  // open: clr
  Register #(.width(32)) register_31 (.D(WriteData), .en(_20), .Q(r20), .clk(c));  // open: clr
  Register #(.width(32)) register_32 (.D(WriteData), .en(_31), .Q(r31), .clk(c));  // open: clr

  // Other names for the same wires on the sheet: data[31:0] = WriteData
endmodule

// control unit
module Control_Unit (
  input  _26__A,
  input  _27__B,
  input  _28__C,
  input  _29__D,
  input  _30__E,
  input  _31__F,
  output Reg_Write,
  output RegDest,
  output aluop1,
  output alu_op2,
  output Branch,
  output Mem_Read,
  output Mem_To_Reg,
  output Mem_write,
  output ALU_src
);

  wire not_1_out, not_2_out, not_3_out, not_4_out, not_5_out, not_6_out;

  not not_1 (not_1_out, _26__A);
  not not_2 (not_2_out, _27__B);
  not not_3 (not_3_out, _28__C);
  not not_4 (not_4_out, _29__D);
  not not_5 (not_5_out, _30__E);
  not not_6 (not_6_out, _31__F);
  and and_1 (aluop1, not_1_out, not_2_out, not_3_out, not_4_out, not_5_out, not_6_out);
  and and_2 (alu_op2, not_1_out, not_2_out, _28__C, not_4_out, not_5_out, not_6_out);
  and and_3 (Mem_Read, not_2_out, not_3_out, not_4_out, _26__A, _30__E, _31__F);
  and and_4 (Mem_write, _26__A, _28__C, _30__E, _31__F, not_2_out, not_4_out);
  or or_1 (ALU_src, Mem_Read, Mem_write);

  assign Branch = alu_op2;
  assign Mem_To_Reg = Mem_Read;
  assign Reg_Write = aluop1;
  assign RegDest = aluop1;
endmodule

module IF_ID (
  input  [31:0] in_1,
  input  [23:0] in_2,
  output [23:0] PC
);

  Register #(.width(32)) INS (.D(in_1));  // open: en, Q, clk, clr
  Register #(.width(24)) u_PC (.D(in_2), .Q(PC));  // open: en, clk, clr
endmodule

module ID_EX (
  input  [23:0] PC,
  input  [31:0] DATA_1,
  input  [31:0] DATA_2,
  input  [31:0] IMM,
  input  [4:0] RT,
  input  [4:0] RD,
  input  [3:0] EX,
  input  [2:0] MEM,
  input  [1:0] WB,
  output [31:0] BRANCH,
  output [4:0] RT_2,
  output [4:0] RD_2,
  output [2:0] MEM_2,
  output [1:0] WB_2
);

  wire [31:0] DATA_1_q, DATA_2_q;

  Register #(.width(24)) u_PC (.D(PC));  // open: en, Q, clk, clr
  Register #(.width(32)) u_DATA_1 (.D(DATA_1), .Q(DATA_1_q));  // open: en, clk, clr
  Register #(.width(32)) u_DATA_2 (.D(DATA_2), .Q(DATA_2_q));  // open: en, clk, clr
  Register #(.width(32)) u_IMM (.D(IMM), .Q(BRANCH));  // open: en, clk, clr
  Register #(.width(5)) u_RT (.D(RT), .Q(RT_2));  // open: en, clk, clr
  Register #(.width(5)) u_RD (.D(RD), .Q(RD_2));  // open: en, clk, clr
  Register #(.width(4)) u_EX (.D(EX));  // open: en, Q, clk, clr
  Register #(.width(3)) u_MEM (.D(MEM), .Q(MEM_2));  // open: en, clk, clr
  Register #(.width(2)) u_WB (.D(WB), .Q(WB_2));  // open: en, clk, clr
endmodule

module EX_MEM (
  input  [2:0] MEM,
  input  [1:0] WB,
  input  [31:0] BRANCH,
  input  ZERO,
  input  [31:0] ALU_RES,
  input  [31:0] in_6,
  input  [4:0] RD,
  output [1:0] WB_2,
  output [31:0] ALU_RES_2,
  output [4:0] RD_2
);

  Register #(.width(3)) u_MEM (.D(MEM));  // open: en, Q, clk, clr
  Register #(.width(2)) u_WB (.D(WB), .Q(WB_2));  // open: en, clk, clr
  Register #(.width(32)) u_BRANCH (.D(BRANCH));  // open: en, Q, clk, clr
  Register #(.width(1)) u_ZERO (.D(ZERO));  // open: en, Q, clk, clr
  Register #(.width(32)) u_ALU_RES (.D(ALU_RES), .Q(ALU_RES_2));  // open: en, clk, clr
  Register #(.width(32)) RT (.D(in_6));  // open: en, Q, clk, clr
  Register #(.width(5)) u_RD (.D(RD), .Q(RD_2));  // open: en, clk, clr
endmodule
